// Logisim project TASK_3.circ as structural Verilog: 1 circuit, main circuit main
module main (
);

  wire and_1_out, clock_1_out, dipswitch_1_sw1, j_k_ff_1_qn, j_k_ff_2_qn, j_k_ff_3_qn, j_k_ff_4_qn,
       j_k_ff_5_qn, j_k_ff_6_qn;

  Clock clock_1 (.out(clock_1_out));
  and and_1 (and_1_out, j_k_ff_1_qn, j_k_ff_2_qn, j_k_ff_3_qn, j_k_ff_4_qn, j_k_ff_5_qn, j_k_ff_6_qn);
  DipSwitch #(.number(2)) dipswitch_1 (.sw1(dipswitch_1_sw1));  // open: sw2
  J_K_Flip_Flop j_k_ff_1 (
    .J(dipswitch_1_sw1), .K(dipswitch_1_sw1), .clk(clock_1_out), .Qn(j_k_ff_1_qn), .preset(and_1_out));  // open: Q, reset
  J_K_Flip_Flop j_k_ff_2 (
    .J(dipswitch_1_sw1), .K(dipswitch_1_sw1), .clk(j_k_ff_1_qn), .Qn(j_k_ff_2_qn), .preset(and_1_out));  // open: Q, reset
  J_K_Flip_Flop j_k_ff_3 (
    .J(dipswitch_1_sw1), .K(dipswitch_1_sw1), .clk(j_k_ff_2_qn), .Qn(j_k_ff_3_qn), .preset(and_1_out));  // open: Q, reset
  J_K_Flip_Flop j_k_ff_4 (
    .J(dipswitch_1_sw1), .K(dipswitch_1_sw1), .clk(j_k_ff_3_qn), .Qn(j_k_ff_4_qn), .reset(and_1_out));  // open: Q, preset
  J_K_Flip_Flop j_k_ff_5 (
    .J(dipswitch_1_sw1), .K(dipswitch_1_sw1), .clk(j_k_ff_4_qn), .Qn(j_k_ff_5_qn), .preset(and_1_out));  // open: Q, reset
  J_K_Flip_Flop j_k_ff_6 (
    .J(dipswitch_1_sw1), .K(dipswitch_1_sw1), .clk(j_k_ff_5_qn), .Qn(j_k_ff_6_qn), .preset(and_1_out));  // open: Q, reset

  // Notes on the sheet:
  //   OBAID 24K-0793
endmodule
