// Logisim project TASK_2.circ as structural Verilog: 1 circuit, main circuit main
module main (
);

  wire clock_1_out, clock_2_out, dipswitch_1_sw1, dipswitch_2_sw1, j_k_ff_1_q, j_k_ff_2_qn, j_k_ff_3_q,
       j_k_ff_4_qn, undriven, undriven_2;

  DipSwitch #(.number(2)) dipswitch_1 (.sw1(dipswitch_1_sw1));  // open: sw2
  Clock clock_1 (.out(clock_1_out));
  DipSwitch #(.number(2)) dipswitch_2 (.sw1(dipswitch_2_sw1));  // open: sw2
  Clock clock_2 (.out(clock_2_out));
  J_K_Flip_Flop j_k_ff_1 (
    .J(dipswitch_1_sw1), .K(dipswitch_1_sw1), .clk(clock_1_out), .Q(j_k_ff_1_q));  // open: Qn, preset, reset
  J_K_Flip_Flop j_k_ff_2 (
    .J(dipswitch_2_sw1), .K(dipswitch_2_sw1), .clk(clock_2_out), .Qn(j_k_ff_2_qn));  // open: Q, preset, reset
  J_K_Flip_Flop j_k_ff_3 (
    .J(dipswitch_1_sw1), .K(dipswitch_1_sw1), .clk(j_k_ff_1_q), .Q(j_k_ff_3_q));  // open: Qn, preset, reset
  J_K_Flip_Flop j_k_ff_4 (
    .J(dipswitch_2_sw1), .K(dipswitch_2_sw1), .clk(j_k_ff_2_qn), .Qn(j_k_ff_4_qn));  // open: Q, preset, reset
  J_K_Flip_Flop j_k_ff_5 (
    .J(dipswitch_1_sw1), .K(dipswitch_1_sw1), .clk(j_k_ff_3_q), .reset(undriven));  // open: Q, Qn, preset
  J_K_Flip_Flop j_k_ff_6 (
    .J(dipswitch_2_sw1), .K(dipswitch_2_sw1), .clk(j_k_ff_4_qn), .reset(undriven_2));  // open: Q, Qn, preset
  // NOT_Gate not_1 is placed but not wired

  // Notes on the sheet:
  //   OBAID 24K-0793
  //   3 bit DOWN Counter
  //   3 bit UP Counter
endmodule
