// Logisim project TASK_2_Updated.circ as structural Verilog: 1 circuit, main circuit main
module main (
);

  wire and_1_out, and_2_out, and_3_out, and_4_out, and_5_out, and_6_out, and_7_out, and_8_out, and_9_out,
       and_10_out, and_11_out, and_12_out, and_13_out, and_14_out, and_15_out, and_16_out, clock_1_out,
       j_k_ff_1_q, j_k_ff_1_qn, j_k_ff_2_q, j_k_ff_2_qn, j_k_ff_3_q, j_k_ff_3_qn, not_1_out, or_1_out,
       or_2_out, or_3_out, or_4_out, or_5_out, or_6_out, Y_sw1;

  DipSwitch #(.number(2)) Y (.sw1(Y_sw1));  // open: sw2
  and and_1 (and_1_out, not_1_out, j_k_ff_3_qn, j_k_ff_2_qn);
  and and_2 (and_2_out, not_1_out, j_k_ff_3_q, j_k_ff_2_q);
  and and_3 (and_3_out, Y_sw1, j_k_ff_3_q, j_k_ff_2_qn);
  and and_4 (and_4_out, Y_sw1, j_k_ff_3_qn, j_k_ff_2_q);
  and and_5 (and_5_out, not_1_out, j_k_ff_3_qn, j_k_ff_2_q);
  and and_6 (and_6_out, not_1_out, j_k_ff_3_q, j_k_ff_2_qn);
  and and_7 (and_7_out, Y_sw1, j_k_ff_3_q, j_k_ff_2_q);
  and and_8 (and_8_out, Y_sw1, j_k_ff_3_qn, j_k_ff_2_qn);
  or or_1 (or_1_out, and_1_out, and_2_out, and_3_out, and_4_out);
  or or_2 (or_2_out, and_5_out, and_6_out, and_7_out, and_8_out);
  Clock clock_1 (.out(clock_1_out));
  not not_1 (not_1_out, Y_sw1);
  J_K_Flip_Flop j_k_ff_1 (
    .J(or_1_out), .K(or_2_out), .clk(clock_1_out), .Q(j_k_ff_1_q), .Qn(j_k_ff_1_qn));  // open: preset, reset
  and and_9 (and_9_out, not_1_out, j_k_ff_3_qn, j_k_ff_1_q);
  and and_10 (and_10_out, Y_sw1, j_k_ff_3_q, j_k_ff_1_q);
  and and_11 (and_11_out, not_1_out, j_k_ff_3_q, j_k_ff_1_q);
  and and_12 (and_12_out, Y_sw1, j_k_ff_3_qn, j_k_ff_1_q);
  or or_3 (or_3_out, and_9_out, and_10_out);
  or or_4 (or_4_out, and_11_out, and_12_out);
  J_K_Flip_Flop j_k_ff_2 (
    .J(or_3_out), .K(or_4_out), .clk(clock_1_out), .Q(j_k_ff_2_q), .Qn(j_k_ff_2_qn));  // open: preset, reset
  and and_13 (and_13_out, Y_sw1, j_k_ff_1_qn, j_k_ff_2_qn);
  and and_14 (and_14_out, not_1_out, j_k_ff_2_q, j_k_ff_1_qn);
  and and_15 (and_15_out, not_1_out, j_k_ff_2_qn, j_k_ff_1_qn);
  and and_16 (and_16_out, Y_sw1, j_k_ff_2_q, j_k_ff_1_qn);
  or or_5 (or_5_out, and_13_out, and_14_out);
  or or_6 (or_6_out, and_15_out, and_16_out);
  J_K_Flip_Flop j_k_ff_3 (
    .J(or_5_out), .K(or_6_out), .clk(clock_1_out), .Q(j_k_ff_3_q), .Qn(j_k_ff_3_qn));  // open: preset, reset

  // Notes on the sheet:
  //   OBAID 24K-0793
endmodule
